// Logisim project ALU.circ as structural Verilog: 1 circuit, main circuit ALU
module ALU (
  input  [31:0] A,
  input  [31:0] B,
  input  [4:0] Shift,
  input  [3:0] Codop,
  input  CarryIn,
  output [31:0] S,
  output [3:0] Flags
);

  wire adc, bitselector_1_out, bitselector_4_out, bitselector_5_out, bitselector_6_out, bitselector_7_out,
       bitselector_8_out, bitselector_12_out, bitselector_13_out, cmn, cmp, cout1, cout2, cout3, cout4, LSL,
       LSR, not_1_out, Nsortie, sa, sb, sbc, subtractor_1_bout, subtractor_2_bout, xnor_1_out, xnor_2_out,
       xnor_3_out, xnor_4_out, xor_1_out, xor_3_out, xor_4_out, xor_5_out;
  wire [4:0] negator_2_out, subtractor_5_out;
  wire [31:0] adder_1_out, adder_4_out, N11, N12, not_2_out, s1, s2, s3, s4, s5, s6, s7, s8, s9, s10, s13,
       s14, s15, s16, subtractor_3_out, subtractor_4_out;

  Adder #(.width(32)) adder_1 (.a(A), .b(B), .out(adder_1_out), .cin(CarryIn));  // open: cout
  BitSelector #(.width(32)) bitselector_1 (.in(adder_1_out), .out(bitselector_1_out), .sel({5{1'b1}}));
  xnor xnor_1 (xnor_1_out, sa, sb);
  xor xor_1 (xor_1_out, sa, bitselector_1_out);
  BitSelector #(.width(32)) bitselector_2 (.in(B), .out(sb), .sel({5{1'b1}}));
  and and_1 (adc, xnor_1_out, xor_1_out);
  assign s1 = A & B;  // AND_Gate and_2, 32 bits wide
  assign s2 = A ^ B;  // XOR_Gate xor_2, 32 bits wide
  Shifter #(.width(32)) shifter_1 (.in(B), .\dist (Shift), .out(s3));
  Shifter #(.shift("lr"), .width(32)) shifter_2 (.in(B), .\dist (Shift), .out(s4));
  Shifter #(.shift("ar"), .width(32)) shifter_3 (.in(B), .\dist (Shift), .out(s5));
  Adder #(.width(32)) adder_2 (.a(B), .b(A), .out(s6), .cin(CarryIn), .cout(cout4));
  not not_1 (not_1_out, CarryIn);
  Subtractor #(.width(32)) subtractor_1 (.a(B), .b(A), .out(s7), .bin(not_1_out), .bout(subtractor_1_bout));
  Shifter #(.shift("rr"), .width(32)) shifter_4 (.in(B), .\dist (Shift), .out(s8));
  Negator #(.width(32)) negator_1 (.in(A), .out(s10));
  Subtractor #(.width(32)) subtractor_2 (.a(B), .b(A), .out(N11), .bin(1'b0), .bout(subtractor_2_bout));
  Adder #(.width(32)) adder_3 (.a(A), .b(B), .out(N12), .cin(1'b0), .cout(cout1));
  Multiplier #(.width(32)) multiplier_1 (.a(A), .b(B), .out(s14));  // open: cin, cout
  assign not_2_out = ~A;  // NOT_Gate not_2, 32 bits wide
  assign s16 = ~B;  // NOT_Gate not_3, 32 bits wide
  BitSelector #(.width(32)) bitselector_3 (.in(A), .out(sa), .sel({5{1'b1}}));
  BitSelector #(.width(32)) bitselector_4 (.in(adder_4_out), .out(bitselector_4_out), .sel({5{1'b1}}));
  Adder #(.width(32)) adder_4 (.a(A), .b(B), .out(adder_4_out));  // open: cin, cout
  not not_4 (cout3, subtractor_1_bout);
  assign s9 = B & A;  // AND_Gate and_3, 32 bits wide
  not not_5 (cout2, subtractor_2_bout);
  assign s13 = A | B;  // OR_Gate or_1, 32 bits wide
  assign s15 = not_2_out & B;  // AND_Gate and_4, 32 bits wide
  xnor xnor_2 (xnor_2_out, sa, sb);
  xor xor_3 (xor_3_out, sa, bitselector_4_out);
  and and_5 (cmn, xnor_2_out, xor_3_out);
  Subtractor #(.width(32)) subtractor_3 (.a(B), .b(A), .out(subtractor_3_out));  // open: bin, bout
  BitSelector #(.width(32)) bitselector_5 (.in(subtractor_3_out), .out(bitselector_5_out), .sel({5{1'b1}}));
  BitSelector #(.width(32)) bitselector_6 (.in(B), .out(bitselector_6_out), .sel({5{1'b1}}));
  xor xor_4 (xor_4_out, sa, sb);
  xnor xnor_3 (xnor_3_out, sa, bitselector_5_out);
  Multiplexer #(.enable("false"), .select(4), .width(32)) multiplexer_1 (
    .in0(s1), .in1(s2), .in2(s3), .in3(s4), .in4(s5), .in5(s6), .in6(s7), .in7(s8), .in8(B), .in9(s10),
    .in10(B), .in11(B), .in12(s13), .in13(s14), .in14(s15), .in15(s16), .out(S), .sel(Codop));
  and and_6 (cmp, xor_4_out, xnor_3_out);
  BitSelector #(.width(32)) bitselector_7 (.in(subtractor_4_out), .out(bitselector_7_out), .sel({5{1'b1}}));
  Subtractor #(.width(32)) subtractor_4 (.a(B), .b(A), .out(subtractor_4_out), .bin(CarryIn));  // open: bout
  Comparator #(.width(32)) comparator_1 (.a(S), .b({32{1'b0}}), .eq(Flags[2]));  // open: gt, lt
  Multiplexer #(.enable("false"), .select(4)) multiplexer_2 (
    .in0(1'b0), .in1(1'b0), .in2(LSL), .in3(LSR), .in4(LSR), .in5(cout4), .in6(cout3),
    .in7(bitselector_6_out), .in8(1'b0), .in9(1'b0), .in10(cout2), .in11(cout1), .in12(1'b0), .in13(1'b0),
    .in14(1'b0), .in15(1'b0), .out(Flags[1]), .sel(Codop));
  Multiplexer #(.enable("false"), .select(4)) multiplexer_3 (
    .in0(1'b0), .in1(1'b0), .in2(1'b0), .in3(1'b0), .in4(1'b0), .in5(adc), .in6(sbc), .in7(1'b0), .in8(1'b0),
    .in9(1'b0), .in10(cmp), .in11(cmn), .in12(1'b0), .in13(1'b0), .in14(1'b0), .in15(1'b0), .out(Flags[0]),
    .sel(Codop));
  xor xor_5 (xor_5_out, sa, sb);
  xnor xnor_4 (xnor_4_out, sa, bitselector_7_out);
  BitSelector #(.width(32)) bitselector_8 (.in(s9), .out(bitselector_8_out), .sel({5{1'b1}}));
  BitSelector #(.width(32)) bitselector_9 (.in(B), .out(LSR), .sel(subtractor_5_out));
  BitSelector #(.width(32)) bitselector_10 (.in(B), .out(LSL), .sel(negator_2_out));
  Negator #(.width(5)) negator_2 (.in(Shift), .out(negator_2_out));
  and and_7 (sbc, xor_5_out, xnor_4_out);
  BitSelector #(.width(32)) bitselector_11 (.in(S), .out(Nsortie), .sel({5{1'b1}}));
  BitSelector #(.width(32)) bitselector_12 (.in(N11), .out(bitselector_12_out), .sel({5{1'b1}}));
  BitSelector #(.width(32)) bitselector_13 (.in(N12), .out(bitselector_13_out), .sel({5{1'b1}}));
  Subtractor #(.width(5)) subtractor_5 (.a(Shift), .b(5'b00001), .out(subtractor_5_out));  // open: bin, bout
  Multiplexer #(.enable("false"), .select(4)) multiplexer_4 (
    .in0(Nsortie), .in1(Nsortie), .in2(Nsortie), .in3(Nsortie), .in4(Nsortie), .in5(Nsortie), .in6(Nsortie),
    .in7(Nsortie), .in8(bitselector_8_out), .in9(Nsortie), .in10(bitselector_12_out),
    .in11(bitselector_13_out), .in12(Nsortie), .in13(Nsortie), .in14(Nsortie), .in15(Nsortie),
    .out(Flags[3]), .sel(Codop));

  // Other names for the same wires on the sheet: V = Flags[0]; C = Flags[1]; Z = Flags[2]; N = Flags[3];
  //   s9bis[31:0] = B; s11[31:0] = B; s12[31:0] = B

  // Notes on the sheet:
  //   Note: for ROR, C = N
  //   Note 2: assume that shift > 0 for LSL and LSR
endmodule
