// Logisim project Ctl_Conditional(1).circ as structural Verilog: 1 circuit, main circuit Conditional
module Conditional (
  input  Enable,
  input  [15:0] Instruction,
  input  Z,
  input  C,
  input  N,
  input  V,
  output [10:0] Offset,
  output Verified
);

  wire AL, CC, comparator_6_eq, comparator_7_eq, comparator_8_eq, comparator_9_eq, comparator_10_eq,
       comparator_11_eq, comparator_12_eq, comparator_13_eq, comparator_14_eq, comparator_15_eq,
       comparator_17_eq, comparator_18_eq, comparator_19_eq, comparator_20_eq, comparator_21_eq,
       comparator_22_eq, comparator_23_eq, comparator_24_eq, comparator_25_eq, conditionalBranch, CS, EQ, GE,
       GT, HI, LE, LS, LT, MI, NE, not_1_out, not_2_out, not_3_out, not_4_out, not_5_out, not_6_out,
       not_8_out, not_9_out, not_10_out, or_1_out, or_2_out, PL, signeC, signeN, signeV, signeZ, TjrFaux, VC,
       verif, VS;
  wire [3:0] cond, cond1011;
  wire [7:0] bitselector_3_out, imm8;
  wire [10:0] bit_extender_1_out, imm11;

  Comparator #(.width(1)) comparator_1 (.a(Z), .b(1'b1), .eq(signeZ));  // open: gt, lt
  Comparator #(.width(1)) comparator_2 (.a(C), .b(1'b1), .eq(signeC));  // open: gt, lt
  Comparator #(.width(1)) comparator_3 (.a(N), .b(1'b1), .eq(signeN));  // open: gt, lt
  Comparator #(.width(1)) comparator_4 (.a(V), .b(1'b1), .eq(signeV));  // open: gt, lt
  BitSelector #(.group(11), .width(16)) bitselector_1 (.in(Instruction), .out(imm11), .sel(1'b0));
  BitSelector #(.group(8), .width(16)) bitselector_2 (.in(Instruction), .out(imm8), .sel(1'b0));
  BitSelector #(.group(8), .width(16)) bitselector_3 (.in(Instruction), .out(bitselector_3_out), .sel(1'b1));
  BitSelector #(.group(4)) bitselector_4 (.in(bitselector_3_out), .out(cond), .sel(1'b0));
  BitSelector #(.group(4)) bitselector_5 (.in(bitselector_3_out), .out(cond1011), .sel(1'b1));
  Comparator #(.width(4)) comparator_5 (.a(cond1011), .b(4'b1101), .eq(conditionalBranch));  // open: gt, lt
  assign bit_extender_1_out = {{3{1'b0}}, imm8};  // Bit_Extender bit_extender_1
  Comparator #(.width(4)) comparator_6 (.a(cond), .b(4'b0000), .eq(comparator_6_eq));  // open: gt, lt
  Comparator #(.width(4)) comparator_7 (.a(cond), .b(4'b0001), .eq(comparator_7_eq));  // open: gt, lt
  Comparator #(.width(4)) comparator_8 (.a(cond), .b(4'b0010), .eq(comparator_8_eq));  // open: gt, lt
  Comparator #(.width(4)) comparator_9 (.a(cond), .b(4'b0011), .eq(comparator_9_eq));  // open: gt, lt
  Comparator #(.width(4)) comparator_10 (.a(cond), .b(4'b0100), .eq(comparator_10_eq));  // open: gt, lt
  Comparator #(.width(4)) comparator_11 (.a(cond), .b(4'b0101), .eq(comparator_11_eq));  // open: gt, lt
  Comparator #(.width(4)) comparator_12 (.a(cond), .b(4'b0110), .eq(comparator_12_eq));  // open: gt, lt
  Comparator #(.width(4)) comparator_13 (.a(cond), .b(4'b0111), .eq(comparator_13_eq));  // open: gt, lt
  Comparator #(.width(4)) comparator_14 (.a(cond), .b(4'b1000), .eq(comparator_14_eq));  // open: gt, lt
  not not_1 (not_1_out, signeZ);
  Comparator #(.width(4)) comparator_15 (.a(cond), .b(4'b1001), .eq(comparator_15_eq));  // open: gt, lt
  not not_2 (not_2_out, signeC);
  or or_1 (or_1_out, not_2_out, signeZ);
  Comparator #(.width(4)) comparator_16 (.a(cond), .b(4'b1110), .eq(AL));  // open: gt, lt
  Multiplexer #(.enable("false"), .width(11)) multiplexer_1 (
    .in0({11{1'b0}}), .in1(bit_extender_1_out), .out(Offset), .sel(Verified));
  Multiplexer #(.enable("false")) multiplexer_2 (.in0(1'b0), .in1(verif), .out(Verified), .sel(Enable));
  and and_1 (EQ, comparator_6_eq, signeZ);
  and and_2 (NE, comparator_7_eq, not_3_out);
  not not_3 (not_3_out, signeZ);
  and and_3 (CS, comparator_8_eq, signeC);
  and and_4 (CC, comparator_9_eq, not_4_out);
  not not_4 (not_4_out, signeC);
  and and_5 (MI, comparator_10_eq, signeN);
  and and_6 (PL, comparator_11_eq, not_5_out);
  not not_5 (not_5_out, signeN);
  and and_7 (VS, comparator_12_eq, signeV);
  and and_8 (VC, comparator_13_eq, not_6_out);
  not not_6 (not_6_out, signeV);
  and and_9 (HI, comparator_14_eq, signeC, not_1_out);
  and and_10 (LS, comparator_15_eq, or_1_out);
  Comparator #(.width(4)) comparator_17 (.a(cond), .b(4'b1010), .eq(comparator_17_eq));  // open: gt, lt
  not not_7 (TjrFaux, comparator_18_eq);
  Comparator #(.width(4)) comparator_18 (.a(cond), .b(4'b1111), .eq(comparator_18_eq));  // open: gt, lt
  and and_11 (GE, comparator_17_eq, comparator_19_eq);
  Comparator #(.width(1)) comparator_19 (.a(signeN), .b(signeV), .eq(comparator_19_eq));  // open: gt, lt
  Comparator #(.width(4)) comparator_20 (.a(cond), .b(4'b1011), .eq(comparator_20_eq));  // open: gt, lt
  not not_8 (not_8_out, comparator_21_eq);
  Comparator #(.width(1)) comparator_21 (.a(signeN), .b(signeV), .eq(comparator_21_eq));  // open: gt, lt
  and and_12 (LT, comparator_20_eq, not_8_out);
  Comparator #(.width(4)) comparator_22 (.a(cond), .b(4'b1100), .eq(comparator_22_eq));  // open: gt, lt
  not not_9 (not_9_out, signeZ);
  Comparator #(.width(1)) comparator_23 (.a(signeN), .b(signeV), .eq(comparator_23_eq));  // open: gt, lt
  Comparator #(.width(4)) comparator_24 (.a(cond), .b(4'b1101), .eq(comparator_24_eq));  // open: gt, lt
  not not_10 (not_10_out, comparator_25_eq);
  Comparator #(.width(1)) comparator_25 (.a(signeN), .b(signeV), .eq(comparator_25_eq));  // open: gt, lt
  and and_13 (GT, comparator_22_eq, not_9_out, comparator_23_eq);
  and and_14 (LE, comparator_24_eq, or_2_out);
  or or_2 (or_2_out, signeZ, not_10_out);
  Multiplexer #(.enable("false"), .select(4)) multiplexer_3 (
    .in0(EQ), .in1(NE), .in2(CS), .in3(CC), .in4(MI), .in5(PL), .in6(VS), .in7(VC), .in8(HI), .in9(LS),
    .in10(GE), .in11(LT), .in12(GT), .in13(LE), .in14(AL), .in15(TjrFaux), .out(verif), .sel(cond));

  // Other names for the same wires on the sheet: instru[15:0] = Instruction

  // Notes on the sheet:
  //   1101 = conditionnal // 11100 unconditionnal
  //   si condition, enable et si c'est une conditional branch = 1 alors verified
  //   Si n'est pas une branch / condition non vérifiées alors 0
  //   si conditionnal branch offset = imm8 sinon offset = imm11
endmodule
