// Logisim project Ctl_Load_Store.circ as structural Verilog: 1 circuit, main circuit Load_Store
module Load_Store (
  input  [15:0] Instruction,
  input  Enable,
  input  Clk,
  input  Reset,
  input  [31:0] Stack_Pointer,
  output Store,
  output Load,
  output PC_Hold,
  output [2:0] Rmd,
  output [31:0] RAM_Addr
);

  wire not_1_out, sortiePC, xor_1_out;
  wire [7:0] bitselector_1_out;
  wire [31:0] bit_extender_1_out, sortieram;

  Multiplexer #(.enable("false"), .width(3)) multiplexer_1 (
    .in0(3'b000), .in1(Instruction[10:8]), .out(Rmd), .sel(Enable));
  BitSelector #(.group(8), .width(16)) bitselector_1 (.in(Instruction), .out(bitselector_1_out), .sel(1'b0));
  Multiplexer #(.enable("false")) multiplexer_2 (.in0(1'b0), .in1(not_1_out), .out(Store), .sel(Enable));
  not not_1 (not_1_out, Instruction[11]);
  assign bit_extender_1_out = {{24{1'b0}}, bitselector_1_out};  // Bit_Extender bit_extender_1
  Adder #(.width(32)) adder_1 (.a(bit_extender_1_out), .b(Stack_Pointer), .out(sortieram));  // open: cin, cout
  Multiplexer #(.enable("false")) multiplexer_3 (.in0(1'b0), .in1(sortiePC), .out(PC_Hold), .sel(Enable));
  xor xor_1 (xor_1_out, sortiePC, Load);
  Multiplexer #(.enable("false")) multiplexer_4 (.in0(1'b0), .in1(Instruction[11]), .out(Load), .sel(Enable));
  D_Flip_Flop d_ff_1 (.D(xor_1_out), .clk(Clk), .Q(sortiePC), .reset(Reset));  // open: Qn, preset
  Multiplexer #(.enable("false"), .width(32)) multiplexer_5 (
    .in0({32{1'b0}}), .in1(sortieram), .out(RAM_Addr), .sel(Enable));

  // Other names for the same wires on the sheet: instru[15:0] = Instruction; bit11 = Instruction[11]; pc = PC_Hold;
  //   ram[31:0] = RAM_Addr

  // Notes on the sheet:
  //   Instruction: pull=down
  //   Delay load and hold PC for 1 cycle for the RAM to send out requested data 
endmodule
