// Logisim project Ctl_Shift_Add_Sub_Mov.circ as structural Verilog: 1 circuit, main circuit Shift_Add_Sub_Mov
module Shift_Add_Sub_Mov (
  input  Enable,
  input  [15:0] Instruction,
  output [3:0] Flags_Update_Mask,
  output Carry,
  output Imm32_Enable,
  output [2:0] Rm,
  output [2:0] Rn,
  output [2:0] Rd,
  output [4:0] Imm5,
  output [31:0] Imm32,
  output [3:0] ALU_Opcode
);

  wire ADDimm3, ADDimm8, ADDr, ASR, carry_t, CMP, imm32_enable_t, LSL, LSR, MOV, not_1_out, SUBimm3, SUBimm8,
       SUBr;
  wire [2:0] rd2, rm2, rn2;
  wire [3:0] alu, flags, index;
  wire [4:0] imm5_t;
  wire [31:0] imm32_t, imm32cmp, imm32imm3, imm32mv;

  not not_1 (not_1_out, Enable);
  Multiplexer #(.enable("false"), .select(4)) multiplexer_1 (
    .in0(1'b0), .in1(1'b0), .in2(1'b0), .in3(1'b0), .in4(1'b0), .in5(1'b1), .in6(1'b1), .in7(1'b1),
    .in8(1'b1), .in9(1'b1), .in10(1'b1), .in11(1'b0), .in12(1'b0), .in13(1'b0), .in14(1'b0), .in15(1'b0),
    .out(imm32_enable_t), .sel(index));
  Multiplexer #(.enable("false"), .select(4), .width(4)) multiplexer_2 (
    .in0(4'b0011), .in1(4'b0011), .in2(4'b0100), .in3(4'b0101), .in4(4'b0110), .in5(4'b0101), .in6(4'b0110),
    .in7(4'b1001), .in8(4'b1010), .in9(4'b0101), .in10(4'b0110), .in11(4'b0000), .in12(4'b0000),
    .in13(4'b0000), .in14(4'b0000), .in15(4'b0000), .out(alu), .sel(index));
  Multiplexer #(.enable("false"), .select(4)) multiplexer_3 (
    .in0(1'b0), .in1(1'b0), .in2(1'b0), .in3(1'b0), .in4(1'b1), .in5(1'b0), .in6(1'b1), .in7(1'b0),
    .in8(1'b0), .in9(1'b0), .in10(1'b1), .in11(1'b0), .in12(1'b0), .in13(1'b0), .in14(1'b0), .in15(1'b0),
    .out(carry_t), .sel(index));
  Multiplexer #(.enable("false"), .width(4)) multiplexer_4 (
    .in0(flags), .in1(4'b0000), .out(Flags_Update_Mask), .sel(not_1_out));
  Multiplexer #(.enable("false")) multiplexer_5 (.in0(carry_t), .in1(1'b0), .out(Carry), .sel(not_1_out));
  Multiplexer #(.enable("false")) multiplexer_6 (.in0(imm32_enable_t), .in1(1'b0), .out(Imm32_Enable), .sel(not_1_out));
  Multiplexer #(.enable("false"), .width(3)) multiplexer_7 (.in0(rn2), .in1(3'b000), .out(Rn), .sel(not_1_out));
  Multiplexer #(.enable("false"), .select(4), .width(4)) multiplexer_8 (
    .in0(4'b1110), .in1(4'b1110), .in2(4'b1110), .in3(4'b1111), .in4(4'b1111), .in5(4'b1111), .in6(4'b1111),
    .in7(4'b1100), .in8(4'b1111), .in9(4'b1111), .in10(4'b1111), .in11(4'b0000), .in12(4'b0000),
    .in13(4'b0000), .in14(4'b0000), .in15(4'b0000), .out(flags), .sel(index));
  Multiplexer #(.enable("false"), .width(3)) multiplexer_9 (.in0(rm2), .in1(3'b000), .out(Rm), .sel(not_1_out));
  Multiplexer #(.enable("false"), .width(3)) multiplexer_10 (.in0(rd2), .in1(3'b000), .out(Rd), .sel(not_1_out));
  Multiplexer #(.enable("false"), .width(5)) multiplexer_11 (
    .in0(imm5_t), .in1({5{1'b0}}), .out(Imm5), .sel(not_1_out));
  Multiplexer #(.enable("false"), .width(32)) multiplexer_12 (
    .in0(imm32_t), .in1({32{1'b0}}), .out(Imm32), .sel(not_1_out));
  Multiplexer #(.enable("false"), .width(4)) multiplexer_13 (
    .in0(alu), .in1(4'b0000), .out(ALU_Opcode), .sel(not_1_out));
  Priority_Encoder #(.select(4)) priority_encoder_1 (
    .in0(LSL), .in1(LSR), .in2(ASR), .in3(ADDr), .in4(SUBr), .in5(ADDimm3), .in6(SUBimm3), .in7(MOV),
    .in8(CMP), .in9(ADDimm8), .in10(SUBimm8), .in11(1'b0), .in12(1'b0), .in13(1'b0), .in14(1'b0),
    .in15(1'b0), .out(index), .en_in(Enable));  // open: gs, en_out
  Comparator #(.width(5)) comparator_1 (.a(Instruction[15:11]), .b({5{1'b0}}), .eq(LSL));  // open: gt, lt
  Comparator #(.width(5)) comparator_2 (.a(Instruction[15:11]), .b(5'b00001), .eq(LSR));  // open: gt, lt
  Comparator #(.width(5)) comparator_3 (.a(Instruction[15:11]), .b(5'b00010), .eq(ASR));  // open: gt, lt
  Comparator #(.width(7)) comparator_4 (.a(Instruction[15:9]), .b(7'b0001100), .eq(ADDr));  // open: gt, lt
  Comparator #(.width(7)) comparator_5 (.a(Instruction[15:9]), .b(7'b0001101), .eq(SUBr));  // open: gt, lt
  Multiplexer #(.enable("false"), .select(4), .width(3)) multiplexer_14 (
    .in0(3'b000), .in1(3'b000), .in2(3'b000), .in3(Instruction[8:6]), .in4(Instruction[8:6]), .in5(3'b000),
    .in6(3'b000), .in7(3'b000), .in8(3'b000), .in9(3'b000), .in10(3'b000), .in11(3'b000), .in12(3'b000),
    .in13(3'b000), .in14(3'b000), .in15(3'b000), .out(rm2), .sel(index));
  Multiplexer #(.enable("false"), .select(4), .width(3)) multiplexer_15 (
    .in0(Instruction[5:3]), .in1(Instruction[5:3]), .in2(Instruction[5:3]), .in3(Instruction[5:3]),
    .in4(Instruction[5:3]), .in5(Instruction[5:3]), .in6(Instruction[5:3]), .in7(3'b000), .in8(3'b000),
    .in9(3'b000), .in10(3'b000), .in11(3'b000), .in12(3'b000), .in13(3'b000), .in14(3'b000), .in15(3'b000),
    .out(rn2), .sel(index));
  Multiplexer #(.enable("false"), .select(4), .width(3)) multiplexer_16 (
    .in0(Instruction[2:0]), .in1(Instruction[2:0]), .in2(Instruction[2:0]), .in3(Instruction[2:0]),
    .in4(Instruction[2:0]), .in5(Instruction[2:0]), .in6(Instruction[2:0]), .in7(Instruction[10:8]),
    .in8(Instruction[10:8]), .in9(Instruction[10:8]), .in10(Instruction[10:8]), .in11(3'b000), .in12(3'b000),
    .in13(3'b000), .in14(3'b000), .in15(3'b000), .out(rd2), .sel(index));
  Comparator #(.width(7)) comparator_6 (.a(Instruction[15:9]), .b(7'b0001110), .eq(ADDimm3));  // open: gt, lt
  Comparator #(.width(7)) comparator_7 (.a(Instruction[15:9]), .b(7'b0001111), .eq(SUBimm3));  // open: gt, lt
  Comparator #(.width(5)) comparator_8 (.a(Instruction[15:11]), .b(5'b00100), .eq(MOV));  // open: gt, lt
  Comparator #(.width(5)) comparator_9 (.a(Instruction[15:11]), .b(5'b00101), .eq(CMP));  // open: gt, lt
  Comparator #(.width(5)) comparator_10 (.a(Instruction[15:11]), .b(5'b00110), .eq(ADDimm8));  // open: gt, lt
  Comparator #(.width(5)) comparator_11 (.a(Instruction[15:11]), .b(5'b00111), .eq(SUBimm8));  // open: gt, lt
  Multiplexer #(.enable("false"), .select(4), .width(5)) multiplexer_17 (
    .in0(Instruction[10:6]), .in1(Instruction[10:6]), .in2(Instruction[10:6]), .in3({5{1'b0}}),
    .in4({5{1'b0}}), .in5({5{1'b0}}), .in6({5{1'b0}}), .in7({5{1'b0}}), .in8({5{1'b0}}), .in9({5{1'b0}}),
    .in10({5{1'b0}}), .in11({5{1'b0}}), .in12({5{1'b0}}), .in13({5{1'b0}}), .in14({5{1'b0}}),
    .in15({5{1'b0}}), .out(imm5_t), .sel(index));
  assign imm32imm3 = {{29{1'b0}}, Instruction[8:6]};  // Bit_Extender bit_extender_1
  assign imm32cmp = {{24{1'b0}}, Instruction[7:0]};  // Bit_Extender bit_extender_2
  Negator #(.width(32)) negator_1 (.in(imm32cmp), .out(imm32mv));
  Multiplexer #(.enable("false"), .select(4), .width(32)) multiplexer_18 (
    .in0({32{1'b0}}), .in1({32{1'b0}}), .in2({32{1'b0}}), .in3({32{1'b0}}), .in4({32{1'b0}}),
    .in5(imm32imm3), .in6(imm32imm3), .in7(imm32mv), .in8(imm32cmp), .in9(imm32cmp), .in10(imm32cmp),
    .in11({32{1'b0}}), .in12({32{1'b0}}), .in13({32{1'b0}}), .in14({32{1'b0}}), .in15({32{1'b0}}),
    .out(imm32_t), .sel(index));
  // also tied to GND on the sheet: {imm5_t[0], imm5_t[1], imm5_t[2], imm5_t[3], imm5_t[4]}

  // Other names for the same wires on the sheet: instru[15:0] = Instruction; rdlsl[2:0] = Instruction[2:0];
  //   rnpourtous[2:0] = Instruction[5:3]; imm5lsl[4:0] = Instruction[10:6]; rm_t[2:0] = Instruction[8:6];
  //   rd2mv[2:0] = Instruction[10:8]; operation2[6:0] = Instruction[15:9]; operation[4:0] = Instruction[15:11]

  // Notes on the sheet:
  //   CARRY:OK
  //   FLAG:OK
  //   IMM32NENABLE : OK
  //   Note: ALU uses Rn register for shifts. Use Rn instead of Rm for shifts (immediate) here too
  //   Note 3: Imm32_Enable forces the use of the immediate for Rm register
  //   INDEX:OK
  //   ALU:OK
  //   Note 2: MOV uses RSB ALU opcode with Imm8 reversed so that it is copied to output register
  //   Pull output low on Enable = 0
  //   only ADD and SUB use Rm
  //   Enable carry for SUB since it is reversed in ALU
  //   ALU will use Imm32 instead of Rm
  //   RM:OK
  //   RD:OK
  //   IMM5 :OK
  //   IMM32:FINIT
endmodule
